# Fritzing sketch brownout (saved by Fritzing 1.0.2b)

parts:
  Part1 = Adafruit QT Py ESP32-S3 [part_number=5426]
  Part2 = Adafruit LiPoly Charger BFF for QT Py [part_number="Adafruit #5397"]
  JP1 = Header 4 [package=molex-1x4_lock]
  JP3 = Header 8 [package=1x08_smd]  # not connected
  Part3 = Adafruit USB Isolator [part_number="Adafruit #2107"]  # not connected
  Part4 = Adafruit LPS35HW [part_number="Adafruit #4258"]
  Part5 = Adafruit SHTC3 STEMMA QT [part_number="Adafruit #4636"]

nets:
  GND: Part1.GND, Part4.GND, Part5.GND
  VCC: Part1.3.3V, Part4.VCC, Part5.VCC
  N1: Part1.SDA1, Part4.SDI/SDA, Part5.SDA
  N2: Part1.SCL1, Part4.SCK/SCL, Part5.SCL
  N3: Part2.GND, JP1.4
  N4: Part2.VBAT, JP1.3

notes:
  USB Isolator / Breakout (different part)
  * 5V line switch toggled/Disconnected.
  * usb-A of breakout to usb-c of qtpy.
  * usb-c of breakout to host pc
  Lipo BFF joined to QTPY
  (Headers Male+Female)
  Nordic PPK2 Power Out (4pin Gnd/Vin/Vout/Gnd)
  Logic pins optional (10pin)

custom parts:
  Adafruit QT Py ESP32-S3: The ESP32-S3 has arrived in QT Py format - and what a great way to get started with this powerful new chip from Espressif! With dual 240 MHz cores, WiFi and BLE support, and native USB, this QT Py is great for powering your IoT projects. The ESP32-S3 is a highly-integrated, low-power, 2.4 GHz Wi-Fi System-on-Chip (SoC) solution that now has WiFi and BLE support, built-in native USB as well as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
  Adafruit LiPoly Charger BFF for QT Py: Is your QT Py all alone, lacking a friend to travel the wide world with? When you were a kid you may have learned about the "buddy" system, well this product is kinda like that! A board that will watch your QT Py's back and give it the power and support to wander out past your USB port. This little lipo charger is designed to fit onto the back of any QT Py board, and make it easy for portable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
  Adafruit USB Isolator: This handy little low-cost USB isolator is exactly what you need to provide protection against harmful noise, ground loops, surges, and spikes. Works with any 1.5Mbps (low speed) or 12Mbps (full speed) USB device. Not for high speed USB devices, often used for video cameras (check your product to make sure its low/full compatible) Based on Analog Device's USB isolators It is particularly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
  Adafruit LPS35HW: Sometimes you need to sense pressure in a damp environment. And sometimes you need to know the relative changes in pressure as well as the absolute pressure. For the times you need to do both (or either), the LPS35HW is the pressure sensor for you. Combining protection from water intrusion with support for high precision relative and absolute measurements, this sensor will do what you need.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
  Adafruit SHTC3 STEMMA QT: Sensirion Temperature/Humidity sensors are some of the finest & highest-accuracy devices you can get. And finally, we have some that have a true I2C interface for easy reading. The SHTC3 sensor has an excellent ±2% relative humidity and ±0.2 °C accuracy for most uses. Unlike some earlier SHT sensors, this sensor has a true I2C interface on address 0x70. Unlike some earlier SHT sensors, this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
